# Fritzing sketch Proj01-basic (saved by Fritzing 0.7.4b)
breadboards: 2

parts:
  U1 = Arduino Mega
  Part1 = Arduino Wireless SD Shield  # not connected
  R1 = Rotary Potentiometer (Small) [maximum_resistance=100kΩ]  # not connected
  R2 = Resistor [tolerance=±5% resistance=220 package=THT]  # not connected
  LED1 = LED - 5mm [color="Red (633nm)" package="5 mm [THT]"]  # not connected
  GLCD_128x1 = LCD screen  # not connected
  U2 = XBee  # not connected
  R3 = Trimmer Potentiometer [maximum_resistance=10kΩ package=THT]  # not connected
  R4 = Photocell (LDR) [package=THT]
  R5 = Resistor [tolerance=±5% resistance=220 package=THT]
  T1 = LM35 Temperature Sensor [package="TO92 [THT]"]

nets:
  N1: U1.+5V, R4.pin_1, T1.+Vs
  GND: U1.GND, R5.Pin_1, T1.GND
  N2: U1.A0, T1.Vout
  N3: U1.A1, R4.pin_0, R5.Pin_0
